// Logisim project Teste12_motorpassos.circ as structural Verilog: 4 circuits, main circuit main
module main (
  input  ligdes,
  input  motor,
  input  sentido,
  input  CLK,
  input  RST,
  output y1,
  output y2,
  output y3,
  output y4
);

  wire combinacional_1_ta, combinacional_1_tb, combinacional_1_tc, sequencial_1_qa, sequencial_1_qb,
       sequencial_1_qc;

  COMBINACIONAL combinacional_1 (
    .LIGDES(ligdes), .MOTOR(motor), .SENTIDO(sentido), .Qa(sequencial_1_qa), .Qb(sequencial_1_qb),
    .Qc(sequencial_1_qc), .Ta(combinacional_1_ta), .Tb(combinacional_1_tb), .Tc(combinacional_1_tc), .Y1(y1),
    .Y2(y2), .Y3(y3), .Y4(y4));
  SEQUENCIAL sequencial_1 (
    .Ta(combinacional_1_ta), .Tb(combinacional_1_tb), .Tc(combinacional_1_tc), .CLK(CLK), .RST(RST),
    .Qa(sequencial_1_qa), .Qb(sequencial_1_qb), .Qc(sequencial_1_qc));
endmodule

module SEQUENCIAL (
  input  Ta,
  input  Tb,
  input  Tc,
  input  CLK,
  input  RST,
  output Qa,
  output Qb,
  output Qc
);

  T_Flip_Flop t_ff_1 (.T(Ta), .clk(CLK), .Q(Qa), .reset(RST));  // open: Qn, preset
  T_Flip_Flop t_ff_2 (.T(Tb), .clk(CLK), .Q(Qb), .reset(RST));  // open: Qn, preset
  T_Flip_Flop t_ff_3 (.T(Tc), .clk(CLK), .Q(Qc), .reset(RST));  // open: Qn, preset
endmodule

module COMBINACIONAL (
  input  LIGDES,
  input  MOTOR,
  input  SENTIDO,
  input  Qa,
  input  Qb,
  input  Qc,
  output Ta,
  output Tb,
  output Tc,
  output Y1,
  output Y2,
  output Y3,
  output Y4
);

  wire and_1_out, and_2_out, and_3_out, and_4_out, and_5_out, and_6_out, and_7_out, and_8_out, and_9_out,
       and_10_out, and_11_out, and_12_out, and_13_out, and_14_out, and_15_out, and_16_out, and_17_out,
       and_18_out, and_19_out, and_20_out, and_21_out, and_22_out, and_23_out, and_24_out, and_25_out,
       and_26_out, not_1_out, not_2_out, not_3_out, not_4_out, not_5_out;

  not not_1 (not_1_out, MOTOR);
  not not_2 (not_2_out, SENTIDO);
  not not_3 (not_3_out, Qa);
  not not_4 (not_4_out, Qb);
  not not_5 (not_5_out, Qc);
  and and_1 (and_1_out, LIGDES, MOTOR, not_2_out, not_3_out, not_4_out);
  and and_2 (and_2_out, LIGDES, MOTOR, Qa, not_4_out, not_5_out);
  and and_3 (and_3_out, LIGDES, MOTOR, SENTIDO, not_3_out, Qb, Qc);
  and and_4 (and_4_out, LIGDES, MOTOR, not_2_out, not_3_out, Qb, not_5_out);
  and and_5 (and_5_out, LIGDES, MOTOR, not_2_out, Qa, not_4_out, not_5_out);
  and and_6 (and_6_out, LIGDES, MOTOR, SENTIDO, not_3_out, Qc);
  and and_7 (and_7_out, LIGDES, MOTOR, not_3_out, Qc);
  and and_8 (and_8_out, LIGDES, MOTOR, not_3_out, Qb);
  and and_9 (and_9_out, LIGDES, MOTOR, Qa, not_4_out, not_5_out);
  and and_10 (and_10_out, LIGDES, MOTOR, SENTIDO, not_3_out);
  and and_11 (and_11_out, LIGDES, not_1_out);
  and and_12 (and_12_out, LIGDES, not_2_out, not_3_out, not_4_out);
  and and_13 (and_13_out, LIGDES, not_2_out, not_3_out, not_5_out);
  and and_14 (and_14_out, LIGDES, not_3_out, not_4_out, not_5_out);
  and and_15 (and_15_out, LIGDES, SENTIDO, not_4_out, not_5_out);
  and and_16 (and_16_out, LIGDES, SENTIDO, not_3_out, Qb, Qc);
  and and_17 (and_17_out, LIGDES, MOTOR, not_2_out, not_3_out, Qb);
  and and_18 (and_18_out, LIGDES, MOTOR, SENTIDO, not_3_out, not_4_out);
  and and_19 (and_19_out, LIGDES, MOTOR, SENTIDO, not_4_out, not_5_out);
  and and_20 (and_20_out, LIGDES, MOTOR, not_2_out, not_3_out, Qb, Qc);
  and and_21 (and_21_out, LIGDES, MOTOR, not_2_out, Qa, not_4_out, not_5_out);
  and and_22 (and_22_out, LIGDES, MOTOR, SENTIDO, not_3_out, not_4_out, Qc);
  and and_23 (and_23_out, LIGDES, MOTOR, SENTIDO, not_3_out, Qb, not_5_out);
  and and_24 (and_24_out, LIGDES, MOTOR, not_2_out, not_3_out, not_4_out);
  and and_25 (and_25_out, LIGDES, MOTOR, not_2_out, not_4_out, not_5_out);
  and and_26 (and_26_out, LIGDES, MOTOR, SENTIDO, not_3_out, Qb);
  or or_1 (Ta, and_1_out, and_2_out, and_3_out);
  or or_2 (Tb, and_4_out, and_5_out, and_6_out);
  or or_3 (Tc, and_7_out, and_8_out, and_9_out, and_10_out);
  or or_4 (Y1, and_11_out, and_12_out, and_13_out, and_14_out, and_15_out, and_16_out);
  or or_5 (Y2, and_17_out, and_18_out, and_19_out);
  or or_6 (Y3, and_20_out, and_21_out, and_22_out, and_23_out);
  or or_7 (Y4, and_24_out, and_25_out, and_26_out);
endmodule

module principal (
  input  in_1,
  input  in_2,
  input  in_3,
  input  in_4
);

  wire clock_1_out, main_1_y1, main_1_y2, main_1_y3, main_1_y4;

  Clock clock_1 (.out(clock_1_out));
  LED led_1 (.in(main_1_y1));
  main main_1 (
    .ligdes(in_1), .motor(in_2), .sentido(in_3), .CLK(clock_1_out), .RST(in_4), .y1(main_1_y1),
    .y2(main_1_y2), .y3(main_1_y3), .y4(main_1_y4));
  LED led_2 (.in(main_1_y4));
  LED led_3 (.in(main_1_y3));
  LED led_4 (.in(main_1_y2));
endmodule
